# Fritzing sketch ByteSense (saved by Fritzing 0.9.3b)
breadboards: 1

parts:
  Part1 = Arduino Uno (Rev3) - ICSP
  Photoresistor = PHOTOCELL [package=photocell]
  IR1 = TSOP312.., 314.. [package=THT]
  Microphone = Breakout Board for Electret Microphone
  R3 = Resistor [tolerance=±5% resistance=220 package="0805 [SMD]"]
  Pot = Rotary Potentiometer (Small) [maximum_resistance=10kΩ package=THT]
  3_Axis_Tilt_Sensor = Triple Axis Accelerometer Breakout - ADXL335

nets:
  N1: Part1.A0, 3_Axis_Tilt_Sensor.XOUT
  N2: Part1.A1, Microphone.AUD
  N3: Part1.A2, Photoresistor.P$2, R3.Pin_0
  N4: Part1.A3, Pot.wiper
  N5: Part1.A4/SDA, 3_Axis_Tilt_Sensor.YOUT
  N6: Part1.D13/SCK, IR1.GND
  VCC: Part1.5V, Photoresistor.P$1, IR1.Data, Microphone.VCC, Pot.leg2, 3_Axis_Tilt_Sensor.VCC
  GND: Part1.GND, IR1.Vs, Microphone.GND, R3.Pin_1, Pot.leg1, 3_Axis_Tilt_Sensor.GND
