# Fritzing sketch voltTest-Scheme (saved by Fritzing 0.9.3b)
breadboards: 1

parts:
  Part1 = Arduino Uno (Rev3) - ICSP
  R1 = Resistor [tolerance=±5% resistance=220 package="2512 [SMD]"]
  R2 = Resistor [tolerance=±5% resistance=220 package="2512 [SMD]"]

nets:
  N1: Part1.A3, R1.Pin_1, R2.Pin_0
  N2: Part1.3V3, R2.Pin_1
  N3: Part1.GND, R1.Pin_0

notes:
  In place of the resistor can be any other conductive material.
